// Logisim project PROCESSADOR_TESTE.circ as structural Verilog: 3 circuits, main circuit REGFIEL
// PROCESSOR
module main (
  input  CLEAR,
  output [3:0] VALOR
);

  wire and_1_out, and_2_out, CLK, controlled_buffer_4_out, DATA, LOAD, MOV, or_1_out, or_2_out, STN, STORE,
       STR, undriven;
  wire [2:0] multiplexer_2_out;
  wire [2:1] OP;
  wire [3:0] alu_1_o, controlled_buffer_1_out, controlled_buffer_3_out, Nr, regfiel_1_b, STRN;
  wire [7:0] CONTADOR, END, multiplexer_1_out;
  wire [15:0] rom_1_data;
  wire [15:14] register_1_q;

  Clock clock_1 (.out(CLK));
  Counter counter_1 (.load(1'b0), .count(1'b1), .Q(CONTADOR), .clk(CLK), .clr(1'b0));  // open: D, carry
  Hex_Digit_Display hex_digit_display_1 (.value(CONTADOR[3:0]));  // open: dp
  Hex_Digit_Display hex_digit_display_2 (.value(CONTADOR[7:4]));  // open: dp
  assign controlled_buffer_1_out = STN ? Nr : 4'bz;  // Controlled_Buffer controlled_buffer_1
  assign controlled_buffer_1_out = STR ? STRN : 4'bz;  // Controlled_Buffer controlled_buffer_2
  assign controlled_buffer_3_out = MOV ? END[6:3] : 4'bz;  // Controlled_Buffer controlled_buffer_3
  Multiplexer #(.width(8)) multiplexer_1 (.in0(CONTADOR), .in1(END), .out(multiplexer_1_out), .sel(STORE));  // open: en
  or or_1 (or_1_out, and_2_out, LOAD);
  ROM #(.dataWidth(16)) rom_1 (.addr(CONTADOR), .data(rom_1_data));  // open: sel
  or or_2 (or_2_out, STN, STR);
  assign controlled_buffer_4_out = LOAD ? 1'b1 : 1'bz;  // Controlled_Buffer controlled_buffer_4
  and and_1 (and_1_out, CLK, STORE);
  assign controlled_buffer_3_out = LOAD ? VALOR : 4'bz;  // Controlled_Buffer controlled_buffer_5
  REGFIEL regfiel_1 (
    .INP(controlled_buffer_3_out), .Clock(CLK), .A(STRN), .RA({Nr[0], END[7:6]}), .RD(multiplexer_2_out),
    .B(regfiel_1_b), .RB(END[5:3]), .STORE(STORE), .Rr(Nr[2:0]));
  Multiplexer #(.width(3)) multiplexer_2 (
    .in0(END[2:0]), .in1(Nr[2:0]), .out(multiplexer_2_out), .sel(or_1_out));  // open: en
  and and_2 (and_2_out, STORE, STR);
  xor xor_1 (LOAD, OP[2], OP[1]);
  and and_3 (STN, ~OP[2], undriven);  // AND_Gate
  and and_4 (STR, undriven, OP[2], OP[1]);
  RAM #(.dataWidth(4), .bus("separate")) ram_1 (
    .addr(multiplexer_1_out), .din(controlled_buffer_1_out), .data(VALOR), .str(or_2_out), .clk(and_1_out),
    .ld(controlled_buffer_4_out), .clr(CLEAR));  // open: sel
  assign controlled_buffer_3_out = DATA ? alu_1_o : 4'bz;  // Controlled_Buffer controlled_buffer_6
  Register #(.width(16)) register_1 (
    .D(rom_1_data), .en(1'b1), .Q({register_1_q, OP, Nr, END}), .clk(CLK));  // open: clr
  and and_5 (STORE, register_1_q[14], register_1_q[15], register_1_q[14]);  // AND_Gate
  and and_6 (MOV, register_1_q[15], register_1_q[14], register_1_q[15]);
  ALU alu_1 (.A(STRN), .B(regfiel_1_b), .O(alu_1_o), .OP({OP, Nr[3]}));
  buf and_7 (DATA, ~register_1_q[14]);  // AND_Gate AND_Gate

  // Other names for the same wires on the sheet: LDN[3:0] = VALOR; Rr[2:0] = Nr[2:0]; NUM[3:0] = END[6:3];
  //   RB[2:0] = END[5:3]; RA[2:0] = {Nr[0], END[7:6]}; OP[0] = Nr[3]; RD[2:0] = END[2:0]

  // Notes on the sheet:
  //   contents of rom_1 (hex, n*v repeats v):
  //   c010 c019 a 3844 c00d 8a05 8402 a005 a102 b000 b101
  //   c010, c019, 000a, 3844, c00d, 282e, 3184
  //   8004
  //   LOAD RB(Ram0), RD(R4)
  //   LOAD LER DA RAM E JOGAR NO REG
  //   10xx xxxx xx00 0100
endmodule

// REGFILE
module REGFIEL (
  input  [3:0] INP,
  input  Clock,
  input  STORE,
  input  [2:0] RA,
  input  [2:0] Rr,
  input  [2:0] RD,
  input  [2:0] RB,
  output [3:0] A,
  output [3:0] B
);

  wire demultiplexer_1_out0, demultiplexer_1_out1, demultiplexer_1_out2, demultiplexer_1_out3,
       demultiplexer_1_out4, demultiplexer_1_out5, demultiplexer_1_out6, demultiplexer_1_out7;
  wire [2:0] multiplexer_3_out;
  wire [3:0] R1_q, R2_q, R3_q, R4_q, R5_q, R6_q, R7_q, RO_q;

  Demultiplexer #(.select(3), .enable("true")) demultiplexer_1 (
    .out0(demultiplexer_1_out0), .out1(demultiplexer_1_out1), .out2(demultiplexer_1_out2),
    .out3(demultiplexer_1_out3), .out4(demultiplexer_1_out4), .out5(demultiplexer_1_out5),
    .out6(demultiplexer_1_out6), .out7(demultiplexer_1_out7), .in(1'b1), .sel(RD));  // open: en
  Register #(.width(4)) RO (.D(INP), .en(demultiplexer_1_out0), .Q(RO_q), .clk(Clock));  // open: clr
  Register #(.width(4)) R1 (.D(INP), .en(demultiplexer_1_out1), .Q(R1_q), .clk(Clock));  // open: clr
  Register #(.width(4)) R2 (.D(INP), .en(demultiplexer_1_out2), .Q(R2_q), .clk(Clock));  // open: clr
  Register #(.width(4)) R3 (.D(INP), .en(demultiplexer_1_out3), .Q(R3_q), .clk(Clock));  // open: clr
  Register #(.width(4)) R4 (.D(INP), .en(demultiplexer_1_out4), .Q(R4_q), .clk(Clock));  // open: clr
  Register #(.width(4)) R5 (.D(INP), .en(demultiplexer_1_out5), .Q(R5_q), .clk(Clock));  // open: clr
  Register #(.width(4)) R6 (.D(INP), .en(demultiplexer_1_out6), .Q(R6_q), .clk(Clock));  // open: clr
  Register #(.width(4)) R7 (.D(INP), .en(demultiplexer_1_out7), .Q(R7_q), .clk(Clock));  // open: clr
  Multiplexer #(.select(3), .width(4)) multiplexer_1 (
    .in0(RO_q), .in1(R1_q), .in2(R2_q), .in3(R3_q), .in4(R4_q), .in5(R5_q), .in6(R6_q), .in7(R7_q), .out(A),
    .sel(multiplexer_3_out));  // open: en
  Multiplexer #(.select(3), .width(4)) multiplexer_2 (
    .in0(RO_q), .in1(R1_q), .in2(R2_q), .in3(R3_q), .in4(R4_q), .in5(R5_q), .in6(R6_q), .in7(R7_q), .out(B),
    .sel(RB));  // open: en
  Multiplexer #(.width(3)) multiplexer_3 (.in0(RA), .in1(Rr), .out(multiplexer_3_out), .sel(STORE));  // open: en
endmodule

module ALU (
  input  [3:0] A,
  input  [3:0] B,
  input  [2:0] OP,
  output [3:0] O
);

  wire [3:0] adder_1_out, and_1_out, multiplier_1_out, or_1_out, shifter_1_out, shifter_2_out,
       subtractor_1_out, xor_1_out;

  Adder #(.width(4)) adder_1 (.a(A), .b(B), .out(adder_1_out), .cin(1'b0));  // open: cout
  Subtractor #(.width(4)) subtractor_1 (.a(A), .b(B), .out(subtractor_1_out), .bin(1'b0));  // open: bout
  assign and_1_out = A & B;  // AND_Gate and_1, 4 bits wide
  assign or_1_out = A | B;  // OR_Gate or_1, 4 bits wide
  assign xor_1_out = A ^ B;  // XOR_Gate xor_1, 4 bits wide
  Shifter #(.width(4)) shifter_1 (.in(A), .\dist (B[1:0]), .out(shifter_1_out));
  Shifter #(.width(4), .shift("lr")) shifter_2 (.in(A), .\dist (B[1:0]), .out(shifter_2_out));
  Multiplier #(.width(4)) multiplier_1 (.a(A), .b(B), .out(multiplier_1_out));  // open: cin, cout
  Multiplexer #(.select(3), .width(4), .enable("true")) multiplexer_1 (
    .in0(adder_1_out), .in1(subtractor_1_out), .in2(and_1_out), .in3(or_1_out), .in4(xor_1_out),
    .in5(shifter_1_out), .in6(shifter_2_out), .in7(multiplier_1_out), .out(O), .sel(OP));  // open: en
endmodule
